// Logisim project 1.circ as structural Verilog: 3 circuits, main circuit main
module main (
);

  wire A, B, C, clock, D, f, g, go, Reset_out, t_ff_1_q, t_ff_2_q, t_ff_3_q, t_ff_4_q;

  Clock clock_1 (.out(clock));
  // Probe on {A, B, C, D}
  T_Flip_Flop t_ff_1 (.clk(clock), .T(1'b1), .Q(t_ff_1_q), .Qn(D), .preset(Reset_out), .en(go));  // open: reset
  // Probe on {A, B, C, D}
  // Probe on f
  T_Flip_Flop t_ff_2 (.clk(t_ff_1_q), .T(1'b1), .Q(t_ff_2_q), .Qn(C), .preset(Reset_out));  // open: reset, en
  // Probe on g
  f f_1 (.A(A), .B(B), .C(C), .D(D), .out_5(f));
  TTY #(.rows(1), .cols(18)) tty_1 (.data({6'b011000, f}), .clk(clock), .we(go), .clr(Reset_out));
  T_Flip_Flop t_ff_3 (.clk(t_ff_2_q), .T(1'b1), .Q(t_ff_3_q), .Qn(B), .preset(Reset_out));  // open: reset, en
  TTY #(.rows(1), .cols(18)) tty_2 (.data({6'b011000, g}), .clk(clock), .we(go), .clr(Reset_out));
  T_Flip_Flop t_ff_4 (.clk(t_ff_3_q), .T(1'b1), .Q(t_ff_4_q), .Qn(A), .preset(Reset_out));  // open: reset, en
  Button Reset (.out(Reset_out));
  T_Flip_Flop t_ff_5 (.clk(t_ff_4_q), .T(1'b1), .Q(go), .preset(Reset_out));  // open: Qn, reset, en
  g g_1 (.A(A), .B(B), .C(C), .D(D), .g(g));

  // Notes on the sheet:
  //   0000111100001011
  //   0000111100001011
endmodule

module f (
  input  A,
  input  B,
  input  C,
  input  D,
  output out_5
);

  wire ABC_out, B_nC_nD_out, nABC_out, nABD_out, not_1_out, not_2_out, not_3_out;

  not not_1 (not_1_out, A);
  not not_2 (not_2_out, C);
  not not_3 (not_3_out, D);
  and B_nC_nD (B_nC_nD_out, B, not_2_out, not_3_out);
  and nABD (nABD_out, not_1_out, B, D);
  and nABC (nABC_out, not_1_out, B, C);
  and ABC (ABC_out, A, B, C);
  or or_1 (out_5, B_nC_nD_out, nABD_out, nABC_out, ABC_out);

  // Notes on the sheet:
  //   Function f
endmodule

module g (
  input  A,
  input  B,
  input  C,
  input  D,
  output g
);

  wire B_nD_out, BC_out, nAB_out, not_1_out, not_2_out;

  not not_1 (not_1_out, A);
  not not_2 (not_2_out, D);
  and nAB (nAB_out, not_1_out, B);
  and BC (BC_out, B, C);
  and B_nD (B_nD_out, B, not_2_out);
  or or_1 (g, nAB_out, BC_out, B_nD_out);
endmodule
