// Logisim project 3.circ as structural Verilog: 1 circuit, main circuit main
module main (
);

  wire A, B, C, clock_1_out, D, E, F, go, Reset_out, t_ff_1_q, t_ff_2_q, t_ff_3_q, t_ff_4_q, t_ff_5_q,
       t_ff_6_q, X0, X1, X2;
  wire [2:0] adder_1_out, adder_2_out, adder_3_out, adder_4_out, adder_5_out, bit_extender_1_out,
       bit_extender_2_out, bit_extender_3_out, bit_extender_4_out, bit_extender_5_out, bit_extender_6_out;

  // Probe on {A, B, C, D, E, F}
  assign bit_extender_1_out = {{2{1'b0}}, A};  // Bit_Extender bit_extender_1
  // Probe on {X2, X1, X0}
  Adder #(.width(3)) adder_1 (.a(bit_extender_1_out), .b(3'b000), .out(adder_1_out));  // open: cin, cout
  TTY #(.rows(1), .cols(65)) tty_1 (.data({4'b0110, X2, X1, X0}), .clk(clock_1_out), .we(go), .clr(Reset_out));
  T_Flip_Flop t_ff_1 (.clk(clock_1_out), .T(1'b1), .Q(t_ff_1_q), .Qn(F), .preset(Reset_out), .en(go));  // open: reset
  Clock clock_1 (.out(clock_1_out));
  assign bit_extender_2_out = {{2{1'b0}}, B};  // Bit_Extender bit_extender_2
  Adder #(.width(3)) adder_2 (.a(bit_extender_2_out), .b(adder_1_out), .out(adder_2_out));  // open: cin, cout
  T_Flip_Flop t_ff_2 (.clk(t_ff_1_q), .T(1'b1), .Q(t_ff_2_q), .Qn(E), .preset(Reset_out));  // open: reset, en
  T_Flip_Flop t_ff_3 (.clk(t_ff_2_q), .T(1'b1), .Q(t_ff_3_q), .Qn(D), .preset(Reset_out));  // open: reset, en
  assign bit_extender_3_out = {{2{1'b0}}, C};  // Bit_Extender bit_extender_3
  Adder #(.width(3)) adder_3 (.a(bit_extender_3_out), .b(adder_2_out), .out(adder_3_out));  // open: cin, cout
  T_Flip_Flop t_ff_4 (.clk(t_ff_3_q), .T(1'b1), .Q(t_ff_4_q), .Qn(C), .preset(Reset_out));  // open: reset, en
  assign bit_extender_4_out = {{2{1'b0}}, D};  // Bit_Extender bit_extender_4
  T_Flip_Flop t_ff_5 (.clk(t_ff_4_q), .T(1'b1), .Q(t_ff_5_q), .Qn(B), .preset(Reset_out));  // open: reset, en
  Adder #(.width(3)) adder_4 (.a(bit_extender_4_out), .b(adder_3_out), .out(adder_4_out));  // open: cin, cout
  T_Flip_Flop t_ff_6 (.clk(t_ff_5_q), .T(1'b1), .Q(t_ff_6_q), .Qn(A), .preset(Reset_out));  // open: reset, en
  assign bit_extender_5_out = {{2{1'b0}}, E};  // Bit_Extender bit_extender_5
  Button Reset (.out(Reset_out));
  T_Flip_Flop t_ff_7 (.clk(t_ff_6_q), .T(1'b1), .Q(go), .preset(Reset_out));  // open: Qn, reset, en
  Adder #(.width(3)) adder_5 (.a(bit_extender_5_out), .b(adder_4_out), .out(adder_5_out));  // open: cin, cout
  assign bit_extender_6_out = {{2{1'b0}}, F};  // Bit_Extender bit_extender_6
  Adder #(.width(3)) adder_6 (.a(bit_extender_6_out), .b(adder_5_out), .out({X2, X1, X0}));  // open: cin, cout

  // Notes on the sheet:
  //   0112122312232334122323342334344512232334233434452334344534454556
endmodule
