// Logisim project 7.circ as structural Verilog: 1 circuit, main circuit main
module main (
);

  wire clock_1_out, d, go, not_1_out, not_2_out, Reset_out, s0, s1, t_ff_1_q, t_ff_2_q, t_ff_3_q, y0, y1, y2,
       y3;

  not not_1 (not_1_out, s1);
  not not_2 (not_2_out, s0);
  // Probe on {s1, s0, d}
  T_Flip_Flop t_ff_1 (.clk(clock_1_out), .T(1'b1), .Q(t_ff_1_q), .Qn(d), .preset(Reset_out), .en(go));  // open: reset
  Clock clock_1 (.out(clock_1_out));
  and and_1 (y0, not_2_out, not_1_out, d);
  and and_2 (y1, s0, not_1_out, d);
  and and_3 (y2, not_2_out, s1, d);
  and and_4 (y3, s0, s1, d);
  T_Flip_Flop t_ff_2 (.clk(t_ff_1_q), .T(1'b1), .Q(t_ff_2_q), .Qn(s1), .preset(Reset_out));  // open: reset, en
  TTY #(.rows(1), .cols(10)) tty_1 (.data({3'b100, y3, y2, y1, y0}), .clk(clock_1_out), .we(go), .clr(Reset_out));
  T_Flip_Flop t_ff_3 (.clk(t_ff_2_q), .T(1'b1), .Q(t_ff_3_q), .Qn(s0), .preset(Reset_out));  // open: reset, en
  Button Reset (.out(Reset_out));
  T_Flip_Flop t_ff_4 (.clk(t_ff_3_q), .T(1'b1), .Q(go), .preset(Reset_out));  // open: Qn, reset, en

  // Notes on the sheet:
  //   @A@D@B@H
endmodule
