// Logisim project test6.circ as structural Verilog: 1 circuit, main circuit main
module main (
);

  wire and_1_out, clock_1_out, multiplexer_1_out, not_1_out, s0, s1, s2, stop, w0, w1, w2, w3, w4, w5, w6,
       w7, y;

  not not_1 (not_1_out, stop);
  // Probe on {w7, w6, w5, w4, w3, w2, w1, w0}
  Counter #(.width(11), .max('h7ff), .ongoal("stay")) counter_1 (
    .Q({w7, w6, w5, w4, w3, w2, w1, w0, s2, s1, s0}), .clk(and_1_out));  // open: load, D, count, carry, clr
  and and_1 (and_1_out, not_1_out, clock_1_out);
  Clock clock_1 (.out(clock_1_out));
  // Probe on {s2, s1, s0}
  Multiplexer #(.select(3)) multiplexer_1 (
    .in0(w0), .in1(w1), .in2(w2), .in3(w3), .in4(w4), .in5(w5), .in6(w6), .in7(w7), .out(multiplexer_1_out),
    .sel({s2, s1, s0}));  // open: en
  xor xor_1 (stop, y, multiplexer_1_out);

  // Notes on the sheet:
  //   In Simulate menu, set tick frequency to 2KHz.
  //   Ctrl-R, then Ctrl-K.  w7-w0 should end up being 11111111, ans s2-s0 111.
  //   If not then there is an error at the given w7-w0, s0-s2 combination.
endmodule
