// Logisim project 4test.circ as structural Verilog: 1 circuit, main circuit main
// A
module main (
);

  wire _4_Counter_carry, A_q, B, BC_out, C, C_qn, CLK, clock_1_out, go, nA, nA_nBw_out, nAB_nw_out, nB,
       not_1_out, or_1_out, Q, Reset_out, w;
  wire [1:0] _4_Counter_q;
  wire [4:0] _32_Counter_q;

  not not_1 (not_1_out, w);
  and nA_nBw (nA_nBw_out, nA, nB, w);
  and nAB_nw (nAB_nw_out, nA, B, not_1_out);
  and BC (BC_out, B, C);
  or or_1 (or_1_out, nA_nBw_out, nAB_nw_out, BC_out);
  D_Flip_Flop A (.clk(CLK), .D(B), .Q(A_q), .Qn(nA));  // open: preset, en, reset
  D_Flip_Flop u_B (.clk(CLK), .D(nA), .Q(B), .Qn(nB));  // open: preset, en, reset
  D_Flip_Flop u_C (.clk(CLK), .D(or_1_out), .Q(C), .Qn(C_qn));  // open: preset, en, reset
  and A_nB_nCw (Q, A_q, nB, C_qn, w);
  TTY #(.rows(17), .cols(4)) tty_1 (.data({6'b011000, Q}), .clk(CLK), .we(go), .clr(Reset_out));
  Button Reset (.out(Reset_out));
  and and_1 (CLK, clock_1_out, go);
  Clock clock_1 (.out(clock_1_out));
  // Probe on _4_Counter_q
  Counter #(.width(2), .max('h3)) _4_Counter (
    .Q(_4_Counter_q), .carry(_4_Counter_carry), .clk(CLK), .clr(Reset_out));  // open: load, D, count
  // Probe on _32_Counter_q[3:0]
  Counter #(.width(5), .max('h1f), .trigger("falling")) _32_Counter (
    .Q(_32_Counter_q), .clk(_4_Counter_carry), .clr(Reset_out));  // open: load, D, count, carry
  // Probe on w
  BitSelector #(.width(4)) bitselector_1 (.in(_32_Counter_q[3:0]), .out(w), .sel(_4_Counter_q));
  not not_2 (go, _32_Counter_q[4]);

  // Notes on the sheet:
  //   11 gates
  //   0000
  //   1000
  //   0100
  //   1100
  //   0010
  //   1010
  //   0110
  //   1110
  //   0001
  //   1001
  //   0101
  //   1101
  //   0011
  //   1011
  //   0111
  //   1111
  //   1
  //   1
endmodule
