// Logisim project 7test.circ as structural Verilog: 1 circuit, main circuit main
module main (
);

  wire A0, A1, A2, A3, Ad0, Ad1, Ad2, Ad3, B0, B1, B2, B3, C0, C1, C2, C3, C4, CIN, clock_1_out, go,
       Reset_out, S0, S1, t_ff_1_q, t_ff_2_q, t_ff_3_q, t_ff_4_q;
  wire [11:11] rom_1_data;

  Clock clock_1 (.out(clock_1_out));
  T_Flip_Flop t_ff_1 (.clk(clock_1_out), .T(1'b1), .Q(t_ff_1_q), .Qn(Ad0), .preset(Reset_out), .en(go));  // open: reset
  // Probe on {C4, C3, C2, C1, C0}
  T_Flip_Flop t_ff_2 (.clk(t_ff_1_q), .T(1'b1), .Q(t_ff_2_q), .Qn(Ad1), .preset(Reset_out));  // open: reset, en
  // Probe on {S1, S0}
  // Probe on CIN
  TTY #(.rows(1), .cols(16)) tty_1 (.data({2'b10, C4, C3, C2, C1, C0}), .clk(clock_1_out), .we(go), .clr(Reset_out));
  T_Flip_Flop t_ff_3 (.clk(t_ff_2_q), .T(1'b1), .Q(t_ff_3_q), .Qn(Ad2), .preset(Reset_out));  // open: reset, en
  ROM #(.addrWidth(4), .dataWidth(12)) rom_1 (
    .addr({Ad3, Ad2, Ad1, Ad0}), .data({rom_1_data[11], CIN, S1, S0, B3, B2, B1, B0, A3, A2, A1, A0}));  // open: sel
  // Probe on {B3, B2, B1, B0}
  T_Flip_Flop t_ff_4 (.clk(t_ff_3_q), .T(1'b1), .Q(t_ff_4_q), .Qn(Ad3), .preset(Reset_out));  // open: reset, en
  // Probe on {rom_1_data[11], CIN, S1, S0, B3, B2, B1, B0, A3, A2, A1, A0}
  // Probe on {A3, A2, A1, A0}
  Button Reset (.out(Reset_out));
  T_Flip_Flop t_ff_5 (.clk(t_ff_4_q), .T(1'b1), .Q(go), .preset(Reset_out));  // open: Qn, reset, en

  // Notes on the sheet:
  //   adds 64 to make printable
  //   contents of rom_1 (hex, n*v repeats v):
  //   0 4ff ac 100 5ff 1ac 200 6ff 2ac 300 7ff 3ac 3c3 73c 37d 7d7
  //   @_X@_^OPS@_VOPTU
endmodule
